// Logisim project ascii-para-braille-pt-br.circ as structural Verilog: 7 circuits, main circuit main
module main (
  input  b7,
  input  b6,
  input  b5,
  input  b4,
  input  b3,
  input  b2,
  input  b1,
  input  b0,
  output P
);

  wire decodificador_de_padroes_de_letras_1__1, decodificador_de_padroes_de_letras_1__2,
       decodificador_de_padroes_de_letras_1__3, decodificador_de_padroes_de_letras_1__4,
       decodificador_de_padroes_de_letras_1__4_m1, decodificador_de_padroes_de_letras_1__5,
       decodificador_de_padroes_de_letras_1__6, decodificador_de_padroes_de_letras_1__6_m1,
       \decodificador_de_padrões_de_prefixo_1_out_5 , \decodificador_de_padrões_de_prefixo_1_out_6 ,
       \decodificador_de_padrões_de_prefixo_1_out_7 , levantador_de_pinos_de_prefixo_1__3,
       levantador_de_pinos_de_prefixo_1__4, levantador_de_pinos_de_prefixo_1__5,
       levantador_de_pinos_de_prefixo_1__6, n4_6_m1_1__4, n4_6_m1_1__6;

  \decodificador_de_padrões_de_prefixo  \decodificador_de_padrões_de_prefixo_1  (
    .b7(b7), .b6(b6), .b5(b5), .b4(b4), .out_5(\decodificador_de_padrões_de_prefixo_1_out_5 ),
    .out_6(\decodificador_de_padrões_de_prefixo_1_out_6 ),
    .out_7(\decodificador_de_padrões_de_prefixo_1_out_7 ));
  levantador_de_pinos_de_prefixo levantador_de_pinos_de_prefixo_1 (
    .in_1(\decodificador_de_padrões_de_prefixo_1_out_7 ),
    .in_2(\decodificador_de_padrões_de_prefixo_1_out_6 ),
    .in_3(\decodificador_de_padrões_de_prefixo_1_out_5 ), ._3(levantador_de_pinos_de_prefixo_1__3),
    ._4(levantador_de_pinos_de_prefixo_1__4), ._5(levantador_de_pinos_de_prefixo_1__5),
    ._6(levantador_de_pinos_de_prefixo_1__6));  // open: m
  LED _1 ();  // open: in
  LED _2 ();  // open: in
  LED _3 (.in(levantador_de_pinos_de_prefixo_1__3));
  LED _4 (.in(n4_6_m1_1__4));
  LED _5 (.in(levantador_de_pinos_de_prefixo_1__5));
  LED _6 (.in(n4_6_m1_1__6));
  decodificador_de_padroes_de_letras decodificador_de_padroes_de_letras_1 (
    .b7(b7), .b6(b6), .b5(b5), .b4(b4), .b3(b3), .b2(b2), .b1(b1), .b0(b0),
    ._1(decodificador_de_padroes_de_letras_1__1), ._2(decodificador_de_padroes_de_letras_1__2),
    ._3(decodificador_de_padroes_de_letras_1__3), ._4(decodificador_de_padroes_de_letras_1__4),
    ._5(decodificador_de_padroes_de_letras_1__5), ._6(decodificador_de_padroes_de_letras_1__6),
    ._4_M1(decodificador_de_padroes_de_letras_1__4_m1), ._6_M1(decodificador_de_padroes_de_letras_1__6_m1));
  _4_6_M1 u_4_6_m1_1 (
    ._4_S1(levantador_de_pinos_de_prefixo_1__6), ._6_S1(levantador_de_pinos_de_prefixo_1__4),
    ._4_S2(decodificador_de_padroes_de_letras_1__6_m1), ._6_S2(decodificador_de_padroes_de_letras_1__4_m1),
    ._4(n4_6_m1_1__4), ._6(n4_6_m1_1__6));
  verificador_paridade verificador_paridade_1 (
    .b7(b7), .b6(b6), .b5(b5), .b4(b4), .b3(b3), .b2(b2), .b1(b1), .b0(b0), .P(P));
  LED _1_2 (.in(decodificador_de_padroes_de_letras_1__1));
  LED _2_2 (.in(decodificador_de_padroes_de_letras_1__2));
  LED _3_2 (.in(decodificador_de_padroes_de_letras_1__3));
  LED _4_2 (.in(decodificador_de_padroes_de_letras_1__4));
  LED _5_2 (.in(decodificador_de_padroes_de_letras_1__5));
  LED _6_2 (.in(decodificador_de_padroes_de_letras_1__6));
endmodule

module \decodificador_de_padrões_de_prefixo  (
  input  b7,
  input  b6,
  input  b5,
  input  b4,
  output out_5,
  output out_6,
  output out_7
);

  wire and_1_out, and_2_out, and_3_out, and_4_out, and_5_out, and_7_out, and_8_out, and_9_out, not_1_out,
       not_2_out, not_3_out, not_4_out, not_5_out, not_6_out, not_7_out, not_8_out, not_9_out, not_10_out,
       not_11_out, not_12_out, not_13_out, not_14_out, not_15_out, not_16_out, not_17_out, or_1_out,
       or_2_out, or_3_out, or_4_out;

  not not_1 (not_1_out, b7);
  not not_2 (not_2_out, b5);
  not not_3 (not_3_out, b4);
  not not_4 (not_4_out, b7);
  not not_5 (not_5_out, b5);
  not not_6 (not_6_out, b6);
  not not_7 (not_7_out, b5);
  not not_8 (not_8_out, b6);
  not not_9 (not_9_out, b5);
  not not_10 (not_10_out, b4);
  not not_11 (not_11_out, b7);
  not not_12 (not_12_out, b6);
  not not_13 (not_13_out, b6);
  not not_14 (not_14_out, b4);
  not not_15 (not_15_out, b7);
  not not_16 (not_16_out, b4);
  not not_17 (not_17_out, b7);
  and and_1 (and_1_out, not_1_out, b6, not_2_out, not_3_out);
  and and_2 (and_2_out, not_4_out, b6, not_5_out, b4);
  and and_3 (and_3_out, b7, not_6_out, not_7_out, b4);
  and and_4 (and_4_out, b7, not_8_out, b5, b4);
  and and_5 (and_5_out, b7, b6, not_9_out, b4);
  and and_6 (out_6, not_11_out, not_12_out, b5, b4);
  and and_7 (and_7_out, b7, not_13_out, b5, not_14_out);
  and and_8 (and_8_out, not_15_out, b6, b5, not_16_out);
  and and_9 (and_9_out, not_17_out, b6, b5, b4);
  or or_1 (or_1_out, and_1_out, and_2_out);
  or or_2 (or_2_out, and_3_out, and_4_out);
  or or_3 (or_3_out, and_7_out, and_8_out);
  or or_4 (or_4_out, or_1_out, or_2_out);
  or or_5 (out_5, or_4_out, and_5_out);
  or or_6 (out_7, or_3_out, and_9_out);

  // Notes on the sheet:
  //   Entradas fora do sub
  //   0100 | A - O MAIUSCULO
  //   0101 | P+ MAIUSCULO
  //   1001| É MAIUSCULO
  //   1011| Â À Á MAIUSCULO
  //   1101| Ê Í MAIUSCULO
  //   1110| Ó Ô Ú MAIUSCULO
  //   0011 | 0 - 9
  //   1010 | á í ó ú MINUSCULO
  //   0110 | a - o MINUSCULO
  //   0111 | p+ MINUSCULO
endmodule

module levantador_de_pinos_de_prefixo (
  input  in_1,
  input  in_2,
  input  in_3,
  output _3,
  output _4,
  output _5,
  output _6,
  output m
);

  wire and_1_out, not_1_out, not_2_out, not_3_out, not_4_out, not_5_out, not_6_out, not_7_out;

  not not_1 (not_1_out, in_2);
  not not_2 (not_2_out, in_1);
  not not_3 (not_3_out, in_3);
  not not_4 (not_4_out, in_1);
  not not_5 (not_5_out, in_3);
  not not_6 (not_6_out, in_2);
  and and_1 (and_1_out, in_3, not_1_out, not_2_out);
  and and_2 (_3, not_3_out, in_2, not_4_out);
  and and_3 (m, not_5_out, not_6_out, in_1);
  not not_7 (not_7_out, _3);
  xnor xnor_1 (_4, and_1_out, not_7_out);

  assign _5 = _3;
  assign _6 = _4;

  // Notes on the sheet:
  //   MAIUSCULAS | 46 (M1)
  //   NUMEROS | 3456 (M1)
  //   MINUSCULOS | NENHUM (M1)
endmodule

module _4_6_M1 (
  input  _4_S1,
  input  _6_S1,
  input  _4_S2,
  input  _6_S2,
  output _4,
  output _6
);

  wire and_1_out, and_2_out, and_3_out, not_1_out, not_2_out, not_3_out, not_4_out, not_5_out, not_6_out,
       xnor_1_out;

  not not_1 (not_1_out, _6_S2);
  not not_2 (not_2_out, _4_S2);
  not not_3 (not_3_out, _6_S1);
  not not_4 (not_4_out, _4_S1);
  and and_1 (and_1_out, _6_S2, _4_S2, _6_S1, _4_S1);
  and and_2 (and_2_out, not_1_out, not_2_out, _6_S1, _4_S1);
  and and_3 (and_3_out, _6_S2, _4_S2, not_3_out, not_4_out);
  not not_5 (not_5_out, and_1_out);
  not not_6 (not_6_out, xnor_1_out);
  xnor xnor_1 (xnor_1_out, not_5_out, and_2_out);
  xnor xnor_2 (_4, not_6_out, and_3_out);

  assign _6 = _4;
endmodule

module decodificador_de_padroes_de_letras (
  input  b3,
  input  b2,
  input  b1,
  input  b0,
  input  b7,
  input  b6,
  input  b5,
  input  b4,
  output _1,
  output _2,
  output _3,
  output _4,
  output _5,
  output _6,
  output _4_M1,
  output _6_M1
);

  wire and_1_out, and_2_out, and_3_out, and_4_out, and_5_out, and_6_out, and_7_out, and_8_out, and_9_out,
       and_10_out, and_11_out, and_12_out, and_13_out, and_14_out, and_15_out, and_16_out, and_17_out,
       and_18_out, and_19_out, and_20_out, and_21_out, and_22_out, and_23_out, and_24_out, and_25_out,
       and_26_out, and_27_out, and_28_out, and_29_out, and_30_out, and_31_out, and_32_out, and_33_out,
       and_34_out, and_35_out, and_36_out, and_37_out, and_38_out, and_39_out, and_40_out, and_41_out,
       and_42_out, and_43_out, and_44_out, and_45_out, and_46_out, and_47_out, and_48_out, and_49_out,
       and_50_out, and_51_out, not_1_out, not_2_out, not_3_out, not_4_out, not_5_out, not_6_out, not_7_out,
       not_8_out, not_9_out, not_10_out, not_11_out, not_12_out, not_13_out, not_14_out, not_15_out,
       not_16_out, not_17_out, not_18_out, not_19_out, not_20_out, not_21_out, not_22_out, not_23_out,
       not_24_out, not_25_out, not_26_out, not_27_out, not_28_out, not_29_out, not_30_out, not_31_out,
       not_32_out, not_33_out, not_34_out, not_35_out, not_36_out, not_37_out, not_38_out, not_39_out,
       not_40_out, not_41_out, not_42_out, not_43_out, not_44_out, not_45_out, not_46_out, not_47_out,
       not_48_out, not_49_out, not_50_out, not_51_out, not_52_out, not_53_out, not_54_out, not_55_out,
       not_56_out, not_57_out, not_58_out, not_59_out, not_60_out, not_61_out, not_62_out, not_63_out,
       not_64_out, not_65_out, not_66_out, not_67_out, not_68_out, not_69_out, not_70_out, not_71_out,
       not_72_out, not_73_out, not_74_out, not_75_out, not_76_out, not_77_out, not_78_out, not_79_out,
       not_80_out, not_81_out, not_82_out, not_83_out, not_84_out, not_85_out, not_86_out, not_87_out,
       not_88_out, not_89_out, not_90_out, not_91_out, not_92_out, not_93_out, not_94_out, not_95_out,
       not_96_out, not_97_out, not_98_out, not_99_out, not_100_out, not_101_out, not_102_out, not_103_out,
       not_104_out, not_105_out, not_106_out, not_107_out, not_108_out, not_109_out, not_110_out,
       not_111_out, not_112_out, not_113_out, not_114_out, not_115_out, not_116_out, not_117_out,
       not_118_out, not_119_out, not_120_out, not_121_out, not_122_out, not_123_out, not_124_out,
       not_125_out, not_126_out, not_127_out, not_128_out, not_129_out, not_130_out, not_131_out,
       not_132_out, not_133_out, not_134_out, not_135_out, not_136_out, not_137_out, not_138_out,
       not_139_out, not_140_out, not_141_out, not_142_out, not_143_out, not_144_out, not_145_out,
       not_146_out, not_147_out, not_148_out, not_149_out, not_150_out, not_151_out, not_152_out,
       not_153_out, not_154_out, not_155_out, not_156_out, not_157_out, not_158_out, not_159_out,
       not_160_out, not_161_out, not_162_out, not_163_out, not_164_out, not_165_out, not_166_out,
       not_167_out, not_168_out, not_169_out, not_170_out, not_171_out, not_172_out, not_173_out,
       not_174_out, not_175_out, not_176_out, not_177_out, not_178_out, not_179_out, not_180_out,
       not_181_out, not_182_out, not_183_out, not_184_out, not_185_out, not_186_out, not_187_out,
       not_188_out, not_189_out, not_190_out, not_191_out, not_192_out, not_193_out, not_194_out,
       not_195_out, not_196_out, not_197_out, not_198_out, not_199_out, not_200_out, not_201_out,
       not_202_out, not_203_out, not_204_out, not_205_out, not_206_out, not_207_out, not_208_out,
       not_209_out, not_210_out, not_211_out, not_212_out, not_213_out, not_214_out, not_215_out,
       not_216_out, not_217_out, not_218_out, not_219_out, not_220_out, not_221_out, not_222_out,
       not_223_out, not_224_out, not_225_out, not_226_out, not_227_out, not_228_out, not_229_out,
       not_230_out, not_231_out, not_232_out, not_233_out, not_234_out, not_235_out, not_236_out,
       not_237_out, not_238_out, not_239_out, not_240_out, not_241_out, not_242_out, not_243_out,
       not_244_out, not_245_out, not_246_out, not_247_out, not_248_out, not_249_out, not_250_out,
       not_251_out, not_252_out, not_253_out, not_254_out, not_255_out, not_256_out, not_257_out,
       not_258_out, not_259_out, not_260_out, not_261_out, not_262_out, not_263_out, not_264_out,
       not_265_out, not_266_out, not_267_out, not_268_out, not_269_out, not_270_out, not_271_out,
       not_272_out, not_273_out, not_274_out, not_275_out, not_276_out, not_277_out, not_278_out,
       not_279_out, not_280_out, not_281_out, not_282_out, not_283_out, not_284_out, not_285_out,
       not_286_out, not_287_out, not_288_out, not_289_out, not_290_out, not_291_out, not_292_out,
       not_293_out, not_294_out, not_295_out, not_296_out, not_297_out, not_298_out, not_299_out,
       not_300_out, not_301_out, not_302_out, not_303_out, not_304_out, not_305_out, not_306_out,
       not_307_out, not_308_out, not_309_out, not_310_out, not_311_out, not_312_out,
       organizador_de_prefixos_para_letras_1_out_5, organizador_de_prefixos_para_letras_1_out_6, xnor_1_out,
       xnor_2_out, xnor_3_out, xnor_4_out, xnor_5_out, xnor_6_out, xnor_7_out, xnor_8_out, xnor_9_out,
       xnor_10_out, xnor_11_out, xnor_12_out, xnor_13_out, xnor_14_out, xnor_15_out, xnor_16_out,
       xnor_17_out, xnor_18_out, xnor_19_out, xnor_20_out, xnor_21_out, xnor_22_out, xnor_23_out,
       xnor_24_out, xnor_25_out, xnor_26_out, xnor_27_out, xnor_28_out, xnor_29_out, xnor_30_out,
       xnor_31_out, xnor_32_out, xnor_33_out, xnor_34_out, xnor_35_out, xnor_36_out, xnor_37_out,
       xnor_38_out, xnor_39_out, xnor_40_out, xnor_41_out, xnor_42_out, xnor_43_out, xnor_44_out,
       xnor_45_out, xnor_46_out, xnor_47_out, xnor_48_out, xnor_49_out, xnor_50_out, xnor_51_out,
       xnor_52_out, xnor_53_out, xnor_54_out, xnor_55_out, xnor_56_out, xnor_57_out, xnor_58_out,
       xnor_59_out, xnor_60_out, xnor_61_out, xnor_62_out, xnor_63_out, xnor_64_out, xnor_65_out,
       xnor_66_out, xnor_67_out, xnor_68_out, xnor_69_out, xnor_70_out, xnor_71_out, xnor_72_out,
       xnor_73_out, xnor_74_out, xnor_75_out, xnor_76_out, xnor_77_out, xnor_78_out, xnor_79_out,
       xnor_80_out, xnor_81_out, xnor_82_out, xnor_83_out, xnor_84_out, xnor_85_out, xnor_86_out,
       xnor_87_out, xnor_88_out, xnor_89_out, xnor_90_out, xnor_91_out, xnor_92_out, xnor_93_out,
       xnor_94_out, xnor_95_out, xnor_96_out, xnor_97_out, xnor_98_out, xnor_99_out, xnor_100_out,
       xnor_101_out, xnor_102_out, xnor_103_out, xnor_104_out, xnor_105_out, xnor_106_out, xnor_107_out,
       xnor_108_out, xnor_109_out, xnor_110_out, xnor_111_out, xnor_112_out, xnor_113_out, xnor_114_out,
       xnor_115_out, xnor_116_out, xnor_117_out, xnor_118_out, xnor_119_out, xnor_120_out, xnor_121_out,
       xnor_122_out, xnor_123_out, xnor_124_out, xnor_126_out, xnor_127_out, xnor_128_out, xnor_129_out,
       xnor_130_out, xnor_131_out, xnor_132_out, xnor_133_out, xnor_134_out, xnor_135_out, xnor_136_out,
       xnor_137_out, xnor_138_out, xnor_140_out, xnor_141_out, xnor_142_out, xnor_144_out, xnor_148_out;

  organizador_de_prefixos_para_letras organizador_de_prefixos_para_letras_1 (
    .b7(b7), .b6(b6), .b5(b5), .b4(b4), .out_5(organizador_de_prefixos_para_letras_1_out_5),
    .out_6(organizador_de_prefixos_para_letras_1_out_6));
  not not_1 (not_1_out, b4);
  not not_2 (not_2_out, b4);
  not not_3 (not_3_out, b4);
  not not_4 (not_4_out, b4);
  not not_5 (not_5_out, b5);
  not not_6 (not_6_out, b0);
  not not_7 (not_7_out, b1);
  not not_8 (not_8_out, b2);
  not not_9 (not_9_out, b3);
  not not_10 (not_10_out, b4);
  not not_11 (not_11_out, b6);
  not not_12 (not_12_out, b5);
  not not_13 (not_13_out, b0);
  not not_14 (not_14_out, b2);
  not not_15 (not_15_out, b3);
  not not_16 (not_16_out, b4);
  not not_17 (not_17_out, b6);
  not not_18 (not_18_out, b5);
  not not_19 (not_19_out, b2);
  not not_20 (not_20_out, b3);
  not not_21 (not_21_out, b6);
  not not_22 (not_22_out, b5);
  not not_23 (not_23_out, b1);
  not not_24 (not_24_out, b3);
  not not_25 (not_25_out, b6);
  not not_26 (not_26_out, b5);
  not not_27 (not_27_out, b3);
  not not_28 (not_28_out, b6);
  not not_29 (not_29_out, b5);
  not not_30 (not_30_out, b0);
  not not_31 (not_31_out, b1);
  not not_32 (not_32_out, b2);
  not not_33 (not_33_out, b6);
  not not_34 (not_34_out, b5);
  not not_35 (not_35_out, b0);
  not not_36 (not_36_out, b1);
  not not_37 (not_37_out, b2);
  not not_38 (not_38_out, b3);
  not not_39 (not_39_out, b6);
  not not_40 (not_40_out, b5);
  not not_41 (not_41_out, b2);
  not not_42 (not_42_out, b3);
  not not_43 (not_43_out, b6);
  not not_44 (not_44_out, b0);
  not not_45 (not_45_out, b1);
  not not_46 (not_46_out, b2);
  not not_47 (not_47_out, b3);
  not not_48 (not_48_out, b4);
  not not_49 (not_49_out, b6);
  not not_50 (not_50_out, b0);
  not not_51 (not_51_out, b2);
  not not_52 (not_52_out, b3);
  not not_53 (not_53_out, b4);
  not not_54 (not_54_out, b6);
  not not_55 (not_55_out, b2);
  not not_56 (not_56_out, b3);
  not not_57 (not_57_out, b4);
  not not_58 (not_58_out, b6);
  not not_59 (not_59_out, b1);
  not not_60 (not_60_out, b3);
  not not_61 (not_61_out, b6);
  not not_62 (not_62_out, b0);
  not not_63 (not_63_out, b3);
  not not_64 (not_64_out, b6);
  not not_65 (not_65_out, b3);
  not not_66 (not_66_out, b6);
  not not_67 (not_67_out, b0);
  not not_68 (not_68_out, b3);
  not not_69 (not_69_out, b4);
  not not_70 (not_70_out, b5);
  not not_71 (not_71_out, b3);
  not not_72 (not_72_out, b4);
  not not_73 (not_73_out, b5);
  not not_74 (not_74_out, b0);
  not not_75 (not_75_out, b2);
  not not_76 (not_76_out, b3);
  not not_77 (not_77_out, b5);
  not not_78 (not_78_out, b1);
  not not_79 (not_79_out, b2);
  not not_80 (not_80_out, b3);
  not not_81 (not_81_out, b4);
  not not_82 (not_82_out, b6);
  not not_83 (not_83_out, b0);
  not not_84 (not_84_out, b3);
  not not_85 (not_85_out, b5);
  not not_86 (not_86_out, b0);
  not not_87 (not_87_out, b1);
  not not_88 (not_88_out, b2);
  not not_89 (not_89_out, b3);
  not not_90 (not_90_out, b4);
  not not_91 (not_91_out, b0);
  not not_92 (not_92_out, b2);
  not not_93 (not_93_out, b3);
  not not_94 (not_94_out, b4);
  not not_95 (not_95_out, b0);
  not not_96 (not_96_out, b1);
  not not_97 (not_97_out, b3);
  not not_98 (not_98_out, b4);
  not not_99 (not_99_out, b1);
  not not_100 (not_100_out, b3);
  not not_101 (not_101_out, b4);
  not not_102 (not_102_out, b1);
  not not_103 (not_103_out, b2);
  not not_104 (not_104_out, b4);
  not not_105 (not_105_out, b1);
  not not_106 (not_106_out, b2);
  not not_107 (not_107_out, b3);
  not not_108 (not_108_out, b0);
  not not_109 (not_109_out, b2);
  not not_110 (not_110_out, b3);
  not not_111 (not_111_out, b2);
  not not_112 (not_112_out, b3);
  not not_113 (not_113_out, b0);
  not not_114 (not_114_out, b1);
  not not_115 (not_115_out, b3);
  not not_116 (not_116_out, b1);
  not not_117 (not_117_out, b3);
  not not_118 (not_118_out, b0);
  not not_119 (not_119_out, b3);
  not not_120 (not_120_out, b3);
  not not_121 (not_121_out, b0);
  not not_122 (not_122_out, b1);
  not not_123 (not_123_out, b2);
  not not_124 (not_124_out, b1);
  not not_125 (not_125_out, b2);
  not not_126 (not_126_out, b0);
  not not_127 (not_127_out, b2);
  not not_128 (not_128_out, b2);
  not not_129 (not_129_out, b0);
  not not_130 (not_130_out, b1);
  not not_131 (not_131_out, b1);
  not not_132 (not_132_out, b0);
  not not_133 (not_133_out, b0);
  not not_134 (not_134_out, b1);
  not not_135 (not_135_out, b2);
  not not_136 (not_136_out, b3);
  not not_137 (not_137_out, b1);
  not not_138 (not_138_out, b2);
  not not_139 (not_139_out, b3);
  not not_140 (not_140_out, b0);
  not not_141 (not_141_out, b2);
  not not_142 (not_142_out, b3);
  not not_143 (not_143_out, b2);
  not not_144 (not_144_out, b3);
  not not_145 (not_145_out, b0);
  not not_146 (not_146_out, b1);
  not not_147 (not_147_out, b3);
  not not_148 (not_148_out, b1);
  not not_149 (not_149_out, b3);
  not not_150 (not_150_out, b0);
  not not_151 (not_151_out, b3);
  not not_152 (not_152_out, b3);
  not not_153 (not_153_out, b0);
  not not_154 (not_154_out, b1);
  not not_155 (not_155_out, b2);
  not not_156 (not_156_out, b1);
  not not_157 (not_157_out, b2);
  not not_158 (not_158_out, b0);
  not not_159 (not_159_out, b2);
  and and_1 (and_1_out, not_5_out, not_6_out, not_7_out, not_8_out, not_9_out, not_10_out, b7, not_11_out);
  and and_2 (and_2_out, not_12_out, not_13_out, b1, not_14_out, not_15_out, not_16_out, b7, not_17_out);
  and and_3 (and_3_out, not_18_out, b0, b1, not_19_out, not_20_out, not_1_out, b7, not_21_out);
  and and_4 (and_4_out, not_22_out, b0, not_23_out, b2, not_24_out, not_2_out, b7, not_25_out);
  and and_5 (and_5_out, not_26_out, b0, b1, b2, not_27_out, not_3_out, b7, not_28_out);
  and and_6 (and_6_out, not_29_out, not_30_out, not_31_out, not_32_out, b3, not_4_out, b7, not_33_out);
  and and_7 (and_7_out, not_34_out, not_35_out, not_36_out, not_37_out, not_38_out, b4, b7, not_39_out);
  and and_8 (and_8_out, not_40_out, b0, b1, not_41_out, not_42_out, b4, b7, not_43_out);
  and and_9 (and_9_out, not_44_out, not_45_out, not_46_out, not_47_out, not_48_out, b5, not_49_out, b7);
  and and_10 (and_10_out, not_50_out, b1, not_51_out, not_52_out, not_53_out, b5, not_54_out, b7);
  and and_11 (and_11_out, b0, b1, not_55_out, not_56_out, not_57_out, b5, not_58_out, b7);
  and and_12 (and_12_out, b0, not_59_out, b2, not_60_out, b4, b5, not_61_out, b7);
  and and_13 (and_13_out, not_62_out, b1, b2, not_63_out, b4, b5, not_64_out, b7);
  and and_14 (and_14_out, b0, b1, b2, not_65_out, b4, b5, not_66_out, b7);
  not not_160 (not_160_out, and_15_out);
  and and_15 (and_15_out, not_67_out, b1, b2, not_68_out, not_69_out, not_70_out, b6, b7);
  and and_16 (and_16_out, b0, b1, b2, not_71_out, not_72_out, not_73_out, b6, b7);
  and and_17 (and_17_out, not_74_out, b1, not_75_out, not_76_out, b4, not_77_out, b6, b7);
  not not_161 (not_161_out, and_18_out);
  and and_18 (and_18_out, b0, not_78_out, not_79_out, not_80_out, not_81_out, b5, not_82_out, b7);
  and and_19 (and_19_out, not_83_out, b1, b2, not_84_out, b4, not_85_out, b6, b7);
  and and_20 (and_20_out, not_86_out, not_87_out, not_88_out, not_89_out, not_90_out, b5, b6, b7);
  and and_21 (and_21_out, not_91_out, b1, not_92_out, not_93_out, not_94_out, b5, b6, b7);
  not not_162 (not_162_out, and_22_out);
  and and_22 (and_22_out, not_95_out, not_96_out, b2, not_97_out, not_98_out, b5, b6, b7);
  and and_23 (and_23_out, b0, not_99_out, b2, not_100_out, not_101_out, b5, b6, b7);
  and and_24 (and_24_out, b0, not_102_out, not_103_out, b3, not_104_out, b5, b6, b7);
  not not_163 (not_163_out, b0);
  not not_164 (not_164_out, b1);
  not not_165 (not_165_out, b2);
  not not_166 (not_166_out, b3);
  and and_25 (and_25_out, b0, not_105_out, not_106_out, not_107_out, organizador_de_prefixos_para_letras_1_out_5);
  and and_26 (and_26_out, not_108_out, b1, not_109_out, not_110_out, organizador_de_prefixos_para_letras_1_out_5);
  and and_27 (and_27_out, b0, b1, not_111_out, not_112_out, organizador_de_prefixos_para_letras_1_out_5);
  and and_28 (and_28_out, not_113_out, not_114_out, b2, not_115_out, organizador_de_prefixos_para_letras_1_out_5);
  and and_29 (and_29_out, b0, not_116_out, b2, not_117_out, organizador_de_prefixos_para_letras_1_out_5);
  and and_30 (and_30_out, not_118_out, b1, b2, not_119_out, organizador_de_prefixos_para_letras_1_out_5);
  and and_31 (and_31_out, b0, b1, b2, not_120_out, organizador_de_prefixos_para_letras_1_out_5);
  and and_32 (and_32_out, not_121_out, not_122_out, not_123_out, b3, organizador_de_prefixos_para_letras_1_out_5);
  and and_33 (and_33_out, b0, not_124_out, not_125_out, b3, organizador_de_prefixos_para_letras_1_out_5);
  and and_34 (and_34_out, not_126_out, b1, not_127_out, b3, organizador_de_prefixos_para_letras_1_out_5);
  and and_35 (and_35_out, b0, b1, not_128_out, b3, organizador_de_prefixos_para_letras_1_out_5);
  and and_36 (and_36_out, not_129_out, not_130_out, b2, b3, organizador_de_prefixos_para_letras_1_out_5);
  and and_37 (and_37_out, b0, not_131_out, b2, b3, organizador_de_prefixos_para_letras_1_out_5);
  and and_38 (and_38_out, not_132_out, b1, b2, b3, organizador_de_prefixos_para_letras_1_out_5);
  and and_39 (and_39_out, b0, b1, b2, b3, organizador_de_prefixos_para_letras_1_out_5);
  and and_40 (and_40_out, not_133_out, not_134_out, not_135_out, not_136_out, organizador_de_prefixos_para_letras_1_out_6);
  and and_41 (and_41_out, b0, not_137_out, not_138_out, not_139_out, organizador_de_prefixos_para_letras_1_out_6);
  and and_42 (and_42_out, not_140_out, b1, not_141_out, not_142_out, organizador_de_prefixos_para_letras_1_out_6);
  and and_43 (and_43_out, b0, b1, not_143_out, not_144_out);
  and and_44 (and_44_out, not_145_out, not_146_out, b2, not_147_out, organizador_de_prefixos_para_letras_1_out_6);
  and and_45 (and_45_out, b0, not_148_out, b2, not_149_out, organizador_de_prefixos_para_letras_1_out_6);
  and and_46 (and_46_out, not_150_out, b1, b2, not_151_out, organizador_de_prefixos_para_letras_1_out_6);
  and and_47 (and_47_out, b0, b1, b2, not_152_out, organizador_de_prefixos_para_letras_1_out_6);
  and and_48 (and_48_out, not_153_out, not_154_out, not_155_out, b3, organizador_de_prefixos_para_letras_1_out_6);
  and and_49 (and_49_out, b0, not_156_out, not_157_out, b3, organizador_de_prefixos_para_letras_1_out_6);
  and and_50 (and_50_out, not_158_out, b1, not_159_out, b3, organizador_de_prefixos_para_letras_1_out_6);
  and and_51 (and_51_out, not_163_out, not_164_out, not_165_out, not_166_out, organizador_de_prefixos_para_letras_1_out_5);
  not not_167 (not_167_out, and_34_out);
  xnor xnor_1 (xnor_1_out, and_51_out, not_167_out);
  not not_168 (not_168_out, and_26_out);
  not not_169 (not_169_out, and_9_out);
  xnor xnor_2 (xnor_2_out, not_160_out, and_16_out);
  xnor xnor_3 (xnor_3_out, not_161_out, and_19_out);
  xnor xnor_4 (xnor_4_out, not_162_out, and_23_out);
  not not_170 (not_170_out, xnor_5_out);
  xnor xnor_5 (xnor_5_out, and_25_out, not_168_out);
  not not_171 (not_171_out, and_27_out);
  not not_172 (not_172_out, and_28_out);
  not not_173 (not_173_out, and_3_out);
  not not_174 (not_174_out, and_4_out);
  not not_175 (not_175_out, and_6_out);
  xnor xnor_6 (xnor_6_out, not_169_out, and_12_out);
  not not_176 (not_176_out, xnor_7_out);
  xnor xnor_7 (xnor_7_out, not_170_out, and_27_out);
  xnor xnor_8 (xnor_8_out, not_171_out, and_28_out);
  xnor xnor_9 (xnor_9_out, not_173_out, and_13_out);
  xnor xnor_10 (xnor_10_out, not_174_out, and_14_out);
  xnor xnor_11 (xnor_11_out, not_175_out, and_17_out);
  not not_177 (not_177_out, and_10_out);
  xnor xnor_12 (xnor_12_out, not_176_out, and_28_out);
  xnor xnor_13 (xnor_13_out, not_172_out, and_29_out);
  not not_178 (not_178_out, and_8_out);
  xnor xnor_14 (xnor_14_out, not_177_out, and_20_out);
  not not_179 (not_179_out, and_11_out);
  not not_180 (not_180_out, xnor_12_out);
  xnor xnor_15 (xnor_15_out, not_178_out, and_21_out);
  xnor xnor_16 (xnor_16_out, not_179_out, and_24_out);
  xnor xnor_17 (xnor_17_out, not_180_out, and_29_out);
  not not_181 (not_181_out, xnor_17_out);
  not not_182 (not_182_out, and_26_out);
  not not_183 (not_183_out, xnor_8_out);
  not not_184 (not_184_out, xnor_18_out);
  xnor xnor_18 (xnor_18_out, not_181_out, and_30_out);
  not not_185 (not_185_out, xnor_19_out);
  xnor xnor_19 (xnor_19_out, not_182_out, and_30_out);
  xnor xnor_20 (xnor_20_out, not_183_out, and_30_out);
  xnor xnor_21 (xnor_21_out, not_184_out, and_31_out);
  xnor xnor_22 (xnor_22_out, not_185_out, and_31_out);
  not not_186 (not_186_out, xnor_20_out);
  not not_187 (not_187_out, xnor_13_out);
  not not_188 (not_188_out, xnor_21_out);
  not not_189 (not_189_out, xnor_22_out);
  xnor xnor_23 (xnor_23_out, not_186_out, and_31_out);
  xnor xnor_24 (xnor_24_out, not_187_out, and_31_out);
  xnor xnor_25 (xnor_25_out, not_188_out, and_32_out);
  xnor xnor_26 (xnor_26_out, not_189_out, and_32_out);
  not not_190 (not_190_out, xnor_24_out);
  not not_191 (not_191_out, xnor_26_out);
  not not_192 (not_192_out, xnor_23_out);
  xnor xnor_27 (xnor_27_out, not_190_out, and_32_out);
  xnor xnor_28 (xnor_28_out, not_191_out, and_33_out);
  xnor xnor_29 (xnor_29_out, not_192_out, and_33_out);
  not not_193 (not_193_out, xnor_28_out);
  not not_194 (not_194_out, xnor_29_out);
  not not_195 (not_195_out, xnor_27_out);
  xnor xnor_30 (xnor_30_out, not_193_out, xnor_1_out);
  xnor xnor_31 (xnor_31_out, not_194_out, xnor_1_out);
  xnor xnor_32 (xnor_32_out, not_195_out, xnor_1_out);
  not not_196 (not_196_out, xnor_25_out);
  not not_197 (not_197_out, xnor_33_out);
  xnor xnor_33 (xnor_33_out, not_196_out, and_35_out);
  xnor xnor_34 (xnor_34_out, not_197_out, and_36_out);
  not not_198 (not_198_out, xnor_30_out);
  not not_199 (not_199_out, and_35_out);
  not not_200 (not_200_out, xnor_34_out);
  xnor xnor_35 (xnor_35_out, not_198_out, and_36_out);
  not not_201 (not_201_out, xnor_31_out);
  not not_202 (not_202_out, xnor_36_out);
  xnor xnor_36 (xnor_36_out, not_199_out, and_36_out);
  xnor xnor_37 (xnor_37_out, not_200_out, and_37_out);
  xnor xnor_38 (xnor_38_out, not_201_out, and_37_out);
  xnor xnor_39 (xnor_39_out, not_202_out, and_37_out);
  not not_203 (not_203_out, xnor_37_out);
  not not_204 (not_204_out, xnor_38_out);
  not not_205 (not_205_out, xnor_32_out);
  not not_206 (not_206_out, xnor_39_out);
  not not_207 (not_207_out, xnor_40_out);
  xnor xnor_40 (xnor_40_out, not_203_out, and_38_out);
  xnor xnor_41 (xnor_41_out, not_204_out, and_38_out);
  xnor xnor_42 (xnor_42_out, not_205_out, and_38_out);
  xnor xnor_43 (xnor_43_out, not_206_out, and_38_out);
  xnor xnor_44 (xnor_44_out, not_207_out, and_39_out);
  not not_208 (not_208_out, xnor_42_out);
  xnor xnor_45 (xnor_45_out, not_208_out, and_39_out);
  not not_209 (not_209_out, xnor_43_out);
  not not_210 (not_210_out, xnor_44_out);
  not not_211 (not_211_out, xnor_35_out);
  not not_212 (not_212_out, xnor_41_out);
  xnor xnor_46 (xnor_46_out, not_209_out, and_39_out);
  xnor xnor_47 (xnor_47_out, not_210_out, and_40_out);
  xnor xnor_48 (xnor_48_out, not_211_out, and_40_out);
  xnor xnor_49 (xnor_49_out, not_212_out, and_40_out);
  not not_213 (not_213_out, xnor_46_out);
  not not_214 (not_214_out, xnor_47_out);
  not not_215 (not_215_out, xnor_48_out);
  not not_216 (not_216_out, xnor_49_out);
  not not_217 (not_217_out, xnor_45_out);
  xnor xnor_50 (xnor_50_out, not_213_out, and_40_out);
  xnor xnor_51 (xnor_51_out, not_214_out, and_41_out);
  xnor xnor_52 (xnor_52_out, not_215_out, and_41_out);
  xnor xnor_53 (xnor_53_out, not_216_out, and_41_out);
  xnor xnor_54 (xnor_54_out, not_217_out, and_41_out);
  not not_218 (not_218_out, xnor_50_out);
  not not_219 (not_219_out, xnor_51_out);
  xnor xnor_55 (xnor_55_out, not_218_out, and_41_out);
  xnor xnor_56 (xnor_56_out, not_219_out, and_42_out);
  not not_220 (not_220_out, xnor_52_out);
  not not_221 (not_221_out, xnor_54_out);
  not not_222 (not_222_out, xnor_55_out);
  not not_223 (not_223_out, xnor_57_out);
  xnor xnor_57 (xnor_57_out, not_220_out, and_42_out);
  xnor xnor_58 (xnor_58_out, not_221_out, and_42_out);
  xnor xnor_59 (xnor_59_out, not_222_out, and_42_out);
  xnor xnor_60 (xnor_60_out, not_223_out, and_43_out);
  not not_224 (not_224_out, xnor_53_out);
  not not_225 (not_225_out, xnor_59_out);
  not not_226 (not_226_out, xnor_61_out);
  xnor xnor_61 (xnor_61_out, not_224_out, and_43_out);
  not not_227 (not_227_out, xnor_58_out);
  not not_228 (not_228_out, xnor_62_out);
  xnor xnor_62 (xnor_62_out, not_225_out, and_43_out);
  not not_229 (not_229_out, xnor_60_out);
  xnor xnor_63 (xnor_63_out, not_229_out, and_44_out);
  xnor xnor_64 (xnor_64_out, not_226_out, and_44_out);
  not not_230 (not_230_out, xnor_64_out);
  xnor xnor_65 (xnor_65_out, not_227_out, and_44_out);
  not not_231 (not_231_out, xnor_56_out);
  not not_232 (not_232_out, xnor_65_out);
  xnor xnor_66 (xnor_66_out, not_228_out, and_44_out);
  xnor xnor_67 (xnor_67_out, not_231_out, and_45_out);
  xnor xnor_68 (xnor_68_out, not_233_out, and_45_out);
  not not_233 (not_233_out, xnor_66_out);
  not not_234 (not_234_out, xnor_67_out);
  not not_235 (not_235_out, xnor_63_out);
  not not_236 (not_236_out, xnor_68_out);
  not not_237 (not_237_out, and_45_out);
  xnor xnor_69 (xnor_69_out, not_234_out, and_46_out);
  xnor xnor_70 (xnor_70_out, not_235_out, and_46_out);
  xnor xnor_71 (xnor_71_out, not_236_out, and_46_out);
  not not_238 (not_238_out, xnor_71_out);
  xnor xnor_72 (xnor_72_out, not_237_out, and_46_out);
  not not_239 (not_239_out, xnor_72_out);
  not not_240 (not_240_out, xnor_70_out);
  xnor xnor_73 (xnor_73_out, not_240_out, and_47_out);
  not not_241 (not_241_out, xnor_74_out);
  xnor xnor_74 (xnor_74_out, not_230_out, and_47_out);
  xnor xnor_75 (xnor_75_out, not_232_out, and_47_out);
  not not_242 (not_242_out, xnor_69_out);
  xnor xnor_76 (xnor_76_out, not_239_out, and_47_out);
  xnor xnor_77 (xnor_77_out, not_242_out, and_48_out);
  xnor xnor_78 (xnor_78_out, not_241_out, and_48_out);
  xnor xnor_79 (xnor_79_out, not_238_out, and_48_out);
  not not_243 (not_243_out, xnor_76_out);
  not not_244 (not_244_out, xnor_77_out);
  xnor xnor_80 (xnor_80_out, not_243_out, and_48_out);
  xnor xnor_81 (xnor_81_out, not_244_out, and_49_out);
  not not_245 (not_245_out, xnor_78_out);
  not not_246 (not_246_out, xnor_75_out);
  not not_247 (not_247_out, xnor_79_out);
  not not_248 (not_248_out, xnor_80_out);
  xnor xnor_82 (xnor_82_out, not_245_out, and_49_out);
  xnor xnor_83 (xnor_83_out, not_246_out, and_49_out);
  xnor xnor_84 (xnor_84_out, not_247_out, and_49_out);
  xnor xnor_85 (xnor_85_out, not_248_out, and_49_out);
  not not_249 (not_249_out, xnor_81_out);
  not not_250 (not_250_out, xnor_83_out);
  not not_251 (not_251_out, xnor_84_out);
  not not_252 (not_252_out, xnor_85_out);
  xnor xnor_86 (xnor_86_out, not_249_out, and_50_out);
  not not_253 (not_253_out, xnor_82_out);
  xnor xnor_87 (xnor_87_out, not_250_out, and_50_out);
  xnor xnor_88 (xnor_88_out, not_251_out, and_50_out);
  xnor xnor_89 (xnor_89_out, not_252_out, and_50_out);
  not not_254 (not_254_out, xnor_86_out);
  not not_255 (not_255_out, xnor_73_out);
  not not_256 (not_256_out, xnor_89_out);
  xnor xnor_90 (xnor_90_out, not_254_out, and_1_out);
  xnor xnor_91 (xnor_91_out, not_255_out, and_1_out);
  xnor xnor_92 (xnor_92_out, not_253_out, and_1_out);
  not not_257 (not_257_out, xnor_88_out);
  xnor xnor_93 (xnor_93_out, not_257_out, and_1_out);
  xnor xnor_94 (xnor_94_out, not_256_out, and_1_out);
  not not_258 (not_258_out, xnor_90_out);
  not not_259 (not_259_out, xnor_91_out);
  not not_260 (not_260_out, xnor_92_out);
  not not_261 (not_261_out, xnor_87_out);
  xnor xnor_95 (xnor_95_out, not_258_out, and_2_out);
  xnor xnor_96 (xnor_96_out, not_259_out, and_2_out);
  xnor xnor_97 (xnor_97_out, not_260_out, and_2_out);
  xnor xnor_98 (xnor_98_out, not_261_out, and_2_out);
  not not_262 (not_262_out, xnor_93_out);
  not not_263 (not_263_out, xnor_94_out);
  not not_264 (not_264_out, xnor_95_out);
  xnor xnor_99 (xnor_99_out, not_262_out, and_2_out);
  xnor xnor_100 (xnor_100_out, not_263_out, and_2_out);
  xnor xnor_101 (xnor_101_out, not_264_out, xnor_9_out);
  not not_265 (not_265_out, xnor_100_out);
  not not_266 (not_266_out, xnor_101_out);
  not not_267 (not_267_out, xnor_96_out);
  not not_268 (not_268_out, xnor_97_out);
  not not_269 (not_269_out, xnor_102_out);
  xnor xnor_102 (xnor_102_out, not_265_out, xnor_9_out);
  xnor xnor_103 (xnor_103_out, not_266_out, xnor_10_out);
  xnor xnor_104 (xnor_104_out, not_267_out, xnor_10_out);
  xnor xnor_105 (xnor_105_out, not_268_out, xnor_10_out);
  xnor xnor_106 (xnor_106_out, not_269_out, xnor_10_out);
  not not_270 (not_270_out, xnor_103_out);
  not not_271 (not_271_out, xnor_104_out);
  not not_272 (not_272_out, xnor_105_out);
  not not_273 (not_273_out, xnor_99_out);
  not not_274 (not_274_out, xnor_106_out);
  xnor xnor_107 (xnor_107_out, not_270_out, and_5_out);
  xnor xnor_108 (xnor_108_out, not_271_out, and_5_out);
  xnor xnor_109 (xnor_109_out, not_272_out, and_5_out);
  xnor xnor_110 (xnor_110_out, not_273_out, and_5_out);
  xnor xnor_111 (xnor_111_out, not_274_out, and_5_out);
  not not_275 (not_275_out, xnor_107_out);
  not not_276 (not_276_out, xnor_108_out);
  not not_277 (not_277_out, xnor_111_out);
  not not_278 (not_278_out, xnor_112_out);
  xnor xnor_112 (xnor_112_out, not_275_out, xnor_11_out);
  xnor xnor_113 (xnor_113_out, not_276_out, xnor_11_out);
  not not_279 (not_279_out, xnor_110_out);
  xnor xnor_114 (xnor_114_out, not_277_out, xnor_11_out);
  xnor xnor_115 (xnor_115_out, not_278_out, and_7_out);
  not not_280 (not_280_out, xnor_113_out);
  not not_281 (not_281_out, xnor_109_out);
  not not_282 (not_282_out, xnor_98_out);
  xnor xnor_116 (xnor_116_out, not_279_out, and_7_out);
  not not_283 (not_283_out, xnor_114_out);
  not not_284 (not_284_out, xnor_115_out);
  xnor xnor_117 (xnor_117_out, not_280_out, and_7_out);
  not not_285 (not_285_out, xnor_118_out);
  xnor xnor_118 (xnor_118_out, not_281_out, and_7_out);
  xnor xnor_119 (xnor_119_out, not_282_out, and_7_out);
  not not_286 (not_286_out, xnor_120_out);
  xnor xnor_120 (xnor_120_out, not_283_out, and_7_out);
  xnor xnor_121 (xnor_121_out, not_284_out, xnor_15_out);
  xnor xnor_122 (xnor_122_out, not_285_out, xnor_15_out);
  not not_287 (not_287_out, xnor_119_out);
  xnor xnor_123 (xnor_123_out, not_286_out, xnor_15_out);
  not not_288 (not_288_out, xnor_121_out);
  not not_289 (not_289_out, xnor_117_out);
  xnor xnor_124 (xnor_124_out, not_287_out, xnor_15_out);
  not not_290 (not_290_out, xnor_116_out);
  not not_291 (not_291_out, xnor_123_out);
  xnor xnor_125 (_1, not_288_out, xnor_6_out);
  xnor xnor_126 (xnor_126_out, not_289_out, xnor_6_out);
  not not_292 (not_292_out, xnor_124_out);
  xnor xnor_127 (xnor_127_out, not_290_out, xnor_6_out);
  xnor xnor_128 (xnor_128_out, not_291_out, xnor_6_out);
  not not_293 (not_293_out, xnor_122_out);
  xnor xnor_129 (xnor_129_out, not_292_out, xnor_6_out);
  not not_294 (not_294_out, xnor_127_out);
  not not_295 (not_295_out, xnor_128_out);
  xnor xnor_130 (xnor_130_out, not_293_out, xnor_14_out);
  xnor xnor_131 (xnor_131_out, not_294_out, xnor_14_out);
  xnor xnor_132 (xnor_132_out, not_295_out, xnor_14_out);
  not not_296 (not_296_out, xnor_126_out);
  not not_297 (not_297_out, xnor_130_out);
  not not_298 (not_298_out, xnor_129_out);
  not not_299 (not_299_out, xnor_131_out);
  not not_300 (not_300_out, xnor_132_out);
  xnor xnor_133 (xnor_133_out, not_296_out, xnor_16_out);
  xnor xnor_134 (xnor_134_out, not_297_out, xnor_16_out);
  xnor xnor_135 (xnor_135_out, not_298_out, xnor_16_out);
  xnor xnor_136 (xnor_136_out, not_299_out, xnor_16_out);
  xnor xnor_137 (xnor_137_out, not_300_out, xnor_16_out);
  not not_301 (not_301_out, xnor_134_out);
  not not_302 (not_302_out, xnor_135_out);
  not not_303 (not_303_out, xnor_136_out);
  not not_304 (not_304_out, and_1_out);
  not not_305 (not_305_out, xnor_138_out);
  xnor xnor_138 (xnor_138_out, not_301_out, xnor_2_out);
  xnor xnor_139 (_5, not_302_out, xnor_2_out);
  xnor xnor_140 (xnor_140_out, not_303_out, xnor_2_out);
  xnor xnor_141 (xnor_141_out, not_304_out, and_16_out);
  xnor xnor_142 (xnor_142_out, not_305_out, xnor_3_out);
  not not_306 (not_306_out, xnor_140_out);
  not not_307 (not_307_out, xnor_141_out);
  not not_308 (not_308_out, xnor_133_out);
  xnor xnor_143 (_3, not_306_out, xnor_3_out);
  xnor xnor_144 (xnor_144_out, not_307_out, and_21_out);
  xnor xnor_145 (_2, not_308_out, xnor_4_out);
  not not_309 (not_309_out, xnor_142_out);
  xnor xnor_146 (_4, not_309_out, xnor_4_out);
  not not_310 (not_310_out, xnor_137_out);
  not not_311 (not_311_out, xnor_144_out);
  xnor xnor_147 (_6, not_310_out, xnor_4_out);
  not not_312 (not_312_out, xnor_148_out);
  xnor xnor_148 (xnor_148_out, not_311_out, and_23_out);
  xnor xnor_149 (_4_M1, not_312_out, and_24_out);

  assign _6_M1 = _4_M1;

  // Notes on the sheet:
  //   â| 16
  //   à | 1246
  //   ê | 126
  //   ô | 1456
  //   ó | 346
  //   ã | 345
  //   Ã | 46 345
  //   õ | 246
  //   Ç | 46 12346
  //   é | 123456
  //   ç | 12346
  //   É | 46 123456
  //   á | 12356
  //   ú |23456
  //   Á | 46 12356
  //   Â | 46 16
  //   À | 46 1246
  //   Ê | 46 126
  //   í | 34
  //   Í | 46 34
  //   Ó | 46 346
  //   Ô | 46 1456
  //   Õ | 46 246
  //   Ú | 46 23456
  //   A | 1
  //   B | 12
  //   C | 14
  //   D | 145
  //   E | 15
  //   F | 124
  //   G | 1245
  //   H | 125
  //   I | 24
  //   J | 245
  //   K | 13
  //   L | 123
  //   M | 134
  //   N | 1345
  //   O | 135
  //   P | 1234
  //   R | 1235
  //   S | 234
  //   T | 2345
  //   U | 136
  //   V | 1236
  //   X | 1346
  //   Y | 13456
  //   Z | 1356
  //   Q | 12345
  //   W | 2456
  //   pinos
  //   1
  //   2
  //   4
  //   5
  //   3
  //   pinos
  //   1
  //   2
  //   4
  //   5
  //   3
endmodule

module organizador_de_prefixos_para_letras (
  input  b7,
  input  b6,
  input  b5,
  input  b4,
  output out_5,
  output out_6
);

  wire and_1_out, and_2_out, and_3_out, and_4_out, and_5_out, not_1_out, not_2_out, not_3_out, not_4_out,
       not_5_out, not_6_out, not_7_out, not_8_out, not_9_out, not_10_out, or_1_out;

  not not_1 (not_1_out, b4);
  not not_2 (not_2_out, b5);
  and and_1 (and_1_out, not_1_out, not_2_out, b6, not_3_out);
  not not_3 (not_3_out, b7);
  not not_4 (not_4_out, b4);
  and and_2 (and_2_out, not_4_out, b5, b6, not_5_out);
  not not_5 (not_5_out, b7);
  and and_3 (and_3_out, b4, b5, not_6_out, not_7_out);
  not not_6 (not_6_out, b6);
  not not_7 (not_7_out, b7);
  not not_8 (not_8_out, b5);
  and and_4 (and_4_out, b4, not_8_out, b6, not_9_out);
  not not_9 (not_9_out, b7);
  and and_5 (and_5_out, b4, b5, b6, not_10_out);
  not not_10 (not_10_out, b7);
  or or_1 (or_1_out, and_1_out, and_2_out);
  or or_2 (out_6, and_4_out, and_5_out);
  or or_3 (out_5, or_1_out, and_3_out);

  // Notes on the sheet:
  //   Entradas fora do sub
  //   - 0100: Maiúsculos
  //   - 0110: Minúsculos
  //   - 0011: Números
  //   - 0101: Maiúsculos
  //   - 0111: Minúsculos
endmodule

module verificador_paridade (
  input  b7,
  input  b6,
  input  b5,
  input  b4,
  input  b3,
  input  b2,
  input  b1,
  input  b0,
  output P
);

  wire xor_1_out, xor_2_out, xor_3_out, xor_4_out, xor_5_out, xor_6_out;

  xor xor_1 (xor_1_out, b6, b7);
  xor xor_2 (xor_2_out, b5, xor_1_out);
  xor xor_3 (xor_3_out, b4, xor_2_out);
  xor xor_4 (xor_4_out, b3, xor_3_out);
  xor xor_5 (xor_5_out, b2, xor_4_out);
  xor xor_6 (xor_6_out, b1, xor_5_out);
  xor xor_7 (P, b0, xor_6_out);
endmodule
