// Logisim project braile.circ as structural Verilog: 4 circuits, main circuit main
module main (
  input  b7,
  input  b6,
  input  b5,
  input  b4,
  input  b3,
  input  b2,
  input  b1,
  input  b0,
  output _1,
  output _4,
  output out_11,
  output out_12,
  output _2,
  output _5,
  output out_15,
  output out_16,
  output _3,
  output _6,
  output out_19,
  output out_20
);

  wire \decodificador_de_padrões_de_prefixo_1_out_5 , \decodificador_de_padrões_de_prefixo_1_out_6 ,
       \decodificador_de_padrões_de_prefixo_1_out_7 , levantador_de_pinos_de_prefixo_1_out_8;

  \decodificador_de_padrões_de_prefixo  \decodificador_de_padrões_de_prefixo_1  (
    .b7(b7), .b6(b6), .b5(b5), .b4(b4), .out_5(\decodificador_de_padrões_de_prefixo_1_out_5 ),
    .out_6(\decodificador_de_padrões_de_prefixo_1_out_6 ),
    .out_7(\decodificador_de_padrões_de_prefixo_1_out_7 ));
  levantador_de_pinos_de_prefixo levantador_de_pinos_de_prefixo_1 (
    .in_1(\decodificador_de_padrões_de_prefixo_1_out_7 ),
    .in_2(\decodificador_de_padrões_de_prefixo_1_out_6 ),
    .in_3(\decodificador_de_padrões_de_prefixo_1_out_5 ), .out_4(_4), .out_5(_6), .out_6(_3), .out_7(_5),
    .out_8(levantador_de_pinos_de_prefixo_1_out_8));
  LED led_1 (.in(levantador_de_pinos_de_prefixo_1_out_8));
  decodificador_de_padroes_de_letras decodificador_de_padroes_de_letras_1 (
    .b4(b4), .b3(b3), .b2(b2), .b1(b1), .b0(b0), .out_6(out_11), .out_7(out_15), .out_8(out_12),
    .out_9(out_16), .out_10(out_19));  // open: out_11

  // Notes on the sheet:
  //   lógica para prefixos
  //   levantador de pinos de prefixo
  //   minusculo
  //   pinos
  //   4
  //   6
  //   3
  //   5
  //   pinos
  //   1
  //   2
  //   4
  //   5
  //   3
endmodule

module \decodificador_de_padrões_de_prefixo  (
  input  b7,
  input  b6,
  input  b5,
  input  b4,
  output out_5,
  output out_6,
  output out_7
);

  wire and_1_out, and_2_out, and_3_out, and_4_out, and_5_out, and_6_out, and_8_out, and_9_out, and_10_out,
       not_1_out, not_2_out, not_3_out, not_4_out, not_5_out, not_6_out, not_7_out, not_8_out, not_9_out,
       not_10_out, not_11_out, not_12_out, not_13_out, not_14_out, not_15_out, not_16_out, not_17_out,
       or_1_out, or_2_out, or_3_out, or_4_out, or_5_out;

  not not_1 (not_1_out, b7);
  not not_2 (not_2_out, b5);
  not not_3 (not_3_out, b4);
  not not_4 (not_4_out, b7);
  not not_5 (not_5_out, b5);
  not not_6 (not_6_out, b6);
  not not_7 (not_7_out, b5);
  not not_8 (not_8_out, b6);
  not not_9 (not_9_out, b5);
  not not_10 (not_10_out, b4);
  not not_11 (not_11_out, b7);
  not not_12 (not_12_out, b6);
  not not_13 (not_13_out, b6);
  not not_14 (not_14_out, b4);
  not not_15 (not_15_out, b7);
  not not_16 (not_16_out, b4);
  not not_17 (not_17_out, b7);
  and and_1 (and_1_out, not_1_out, b6, not_2_out, not_3_out);
  and and_2 (and_2_out, not_4_out, b6, not_5_out, b4);
  and and_3 (and_3_out, b7, not_6_out, not_7_out, b4);
  and and_4 (and_4_out, b7, not_8_out, b5, b4);
  and and_5 (and_5_out, b7, b6, not_9_out, b4);
  and and_6 (and_6_out, b7, b6, b5, not_10_out);
  and and_7 (out_6, not_11_out, not_12_out, b5, b4);
  and and_8 (and_8_out, b7, not_13_out, b5, not_14_out);
  and and_9 (and_9_out, not_15_out, b6, b5, not_16_out);
  and and_10 (and_10_out, not_17_out, b6, b5, b4);
  or or_1 (or_1_out, and_1_out, and_2_out);
  or or_2 (or_2_out, and_3_out, and_4_out);
  or or_3 (or_3_out, and_5_out, and_6_out);
  or or_4 (or_4_out, and_8_out, and_9_out);
  or or_5 (or_5_out, or_1_out, or_2_out);
  or or_6 (out_5, or_5_out, or_3_out);
  or or_7 (out_7, or_4_out, and_10_out);

  // Notes on the sheet:
  //   Entradas fora do sub
  //   0100 | A - O MAIUSCULO
  //   0101 | P+ MAIUSCULO
  //   1001| É MAIUSCULO
  //   1011| Â À Á MAIUSCULO
  //   1101| Ê Í MAIUSCULO
  //   1110| Ó Ô Ú MAIUSCULO
  //   0011 | 0 - 9
  //   1010 | á í ó ú MINUSCULO
  //   0110 | a - o MINUSCULO
  //   0111 | p+ MINUSCULO
endmodule

module levantador_de_pinos_de_prefixo (
  input  in_1,
  input  in_2,
  input  in_3,
  output out_4,
  output out_5,
  output out_6,
  output out_7,
  output out_8
);

  wire and_1_out, not_1_out, not_2_out, not_3_out, not_4_out, not_5_out, not_6_out, not_7_out;

  not not_1 (not_1_out, in_2);
  not not_2 (not_2_out, in_1);
  not not_3 (not_3_out, in_3);
  not not_4 (not_4_out, in_1);
  not not_5 (not_5_out, in_3);
  not not_6 (not_6_out, in_2);
  and and_1 (and_1_out, in_3, not_1_out, not_2_out);
  and and_2 (out_6, not_3_out, in_2, not_4_out);
  and and_3 (out_8, not_5_out, not_6_out, in_1);
  not not_7 (not_7_out, out_6);
  xnor xnor_1 (out_4, and_1_out, not_7_out);

  assign out_5 = out_4;
  assign out_7 = out_6;

  // Notes on the sheet:
  //   MAIUSCULAS | 46 (M1)
  //   NUMEROS | 3456 (M1)
  //   MINUSCULOS | NENHUM (M1)
endmodule

module decodificador_de_padroes_de_letras (
  input  b4,
  input  b3,
  input  b2,
  input  b1,
  input  b0,
  output out_6,
  output out_7,
  output out_8,
  output out_9,
  output out_10,
  output out_11
);

  wire and_1_out, and_2_out, and_3_out, and_4_out, and_5_out, and_6_out, and_7_out, and_8_out, and_9_out,
       and_10_out, and_11_out, and_12_out, and_13_out, and_14_out, and_15_out, and_16_out, and_17_out,
       and_18_out, and_19_out, and_20_out, not_1_out, not_2_out, not_3_out, not_4_out, not_5_out, not_6_out,
       not_7_out, not_8_out, not_9_out, not_10_out, not_11_out, not_12_out, not_13_out, not_14_out,
       not_15_out, not_16_out, not_17_out, not_18_out, not_19_out, not_20_out, not_21_out, not_22_out,
       not_23_out, not_24_out, not_25_out, not_26_out, not_27_out, not_28_out, not_29_out, not_30_out,
       not_31_out, not_32_out, not_33_out, not_34_out, not_35_out, not_36_out, not_37_out, not_38_out,
       not_39_out, not_40_out, not_41_out, not_42_out, not_43_out, not_44_out, not_45_out, not_46_out,
       not_47_out, not_48_out, not_49_out, not_50_out, not_51_out, not_52_out, not_53_out, not_54_out,
       not_55_out, not_56_out, not_57_out, not_58_out, not_59_out, not_60_out, not_61_out, not_62_out,
       not_63_out, not_64_out, not_65_out, not_66_out, not_67_out, not_68_out, not_69_out, not_70_out,
       not_71_out, not_72_out, not_73_out, not_74_out, not_75_out, not_76_out, not_77_out, not_78_out,
       not_79_out, not_80_out, not_81_out, not_82_out, not_83_out, not_84_out, not_85_out, not_86_out,
       not_87_out, not_88_out, not_89_out, not_90_out, not_91_out, not_92_out, not_93_out, not_94_out,
       not_95_out, not_96_out, not_97_out, not_98_out, not_99_out, not_100_out, not_101_out, not_102_out,
       not_103_out, not_104_out, not_105_out, not_106_out, not_107_out, undriven, xnor_1_out, xnor_2_out,
       xnor_4_out, xnor_5_out, xnor_6_out, xnor_7_out, xnor_8_out, xnor_9_out, xnor_10_out, xnor_11_out,
       xnor_12_out, xnor_13_out, xnor_14_out, xnor_15_out, xnor_16_out, xnor_17_out, xnor_18_out,
       xnor_19_out, xnor_20_out, xnor_21_out, xnor_22_out, xnor_23_out, xnor_24_out, xnor_25_out,
       xnor_26_out, xnor_27_out, xnor_28_out, xnor_29_out, xnor_30_out, xnor_31_out, xnor_32_out,
       xnor_33_out, xnor_34_out, xnor_35_out, xnor_36_out, xnor_37_out, xnor_38_out, xnor_39_out,
       xnor_40_out, xnor_41_out, xnor_42_out, xnor_43_out, xnor_44_out, xnor_45_out, xnor_47_out, xnor_49_out;

  not not_1 (not_1_out, b1);
  not not_2 (not_2_out, b4);
  not not_3 (not_3_out, b2);
  not not_4 (not_4_out, b3);
  not not_5 (not_5_out, b0);
  not not_6 (not_6_out, b4);
  not not_7 (not_7_out, b2);
  not not_8 (not_8_out, b3);
  not not_9 (not_9_out, b4);
  not not_10 (not_10_out, b2);
  not not_11 (not_11_out, b3);
  not not_12 (not_12_out, b0);
  not not_13 (not_13_out, b1);
  not not_14 (not_14_out, b4);
  not not_15 (not_15_out, b3);
  not not_16 (not_16_out, b1);
  not not_17 (not_17_out, b4);
  not not_18 (not_18_out, b3);
  not not_19 (not_19_out, b0);
  not not_20 (not_20_out, b4);
  not not_21 (not_21_out, b3);
  not not_22 (not_22_out, b4);
  not not_23 (not_23_out, b3);
  not not_24 (not_24_out, b0);
  not not_25 (not_25_out, b1);
  not not_26 (not_26_out, b4);
  not not_27 (not_27_out, b2);
  not not_28 (not_28_out, b1);
  not not_29 (not_29_out, b4);
  not not_30 (not_30_out, b2);
  not not_31 (not_31_out, b0);
  not not_32 (not_32_out, b4);
  not not_33 (not_33_out, b2);
  not not_34 (not_34_out, b4);
  not not_35 (not_35_out, b2);
  not not_36 (not_36_out, b0);
  not not_37 (not_37_out, b1);
  not not_38 (not_38_out, b4);
  not not_39 (not_39_out, b1);
  not not_40 (not_40_out, b4);
  not not_41 (not_41_out, b0);
  not not_42 (not_42_out, b4);
  not not_43 (not_43_out, b4);
  not not_44 (not_44_out, b0);
  not not_45 (not_45_out, b1);
  not not_46 (not_46_out, b2);
  not not_47 (not_47_out, b3);
  not not_48 (not_48_out, b1);
  not not_49 (not_49_out, b2);
  not not_50 (not_50_out, b3);
  not not_51 (not_51_out, b0);
  not not_52 (not_52_out, b2);
  not not_53 (not_53_out, b3);
  not not_54 (not_54_out, b2);
  not not_55 (not_55_out, b3);
  and and_1 (and_1_out, b0, not_1_out, not_2_out, not_3_out, not_4_out);
  and and_2 (and_2_out, not_5_out, b1, not_6_out, not_7_out, not_8_out);
  and and_3 (and_3_out, b0, b1, not_9_out, not_10_out, not_11_out);
  and and_4 (and_4_out, not_12_out, not_13_out, not_14_out, b2, not_15_out);
  and and_5 (and_5_out, b0, not_16_out, not_17_out, b2, not_18_out);
  and and_6 (and_6_out, not_19_out, b1, not_20_out, b2, not_21_out);
  and and_7 (and_7_out, b0, b1, not_22_out, b2, not_23_out);
  and and_8 (and_8_out, not_24_out, not_25_out, not_26_out, not_27_out, b3);
  and and_9 (and_9_out, b0, not_28_out, not_29_out, not_30_out, b3);
  and and_10 (and_10_out, not_31_out, b1, not_32_out, not_33_out, b3);
  and and_11 (and_11_out, b0, b1, not_34_out, not_35_out, b3);
  and and_12 (and_12_out, not_36_out, not_37_out, not_38_out, b2, b3);
  and and_13 (and_13_out, b0, not_39_out, not_40_out, b2, b3);
  and and_14 (and_14_out, not_41_out, b1, not_42_out, b2, b3);
  and and_15 (and_15_out, b0, b1, not_43_out, b2, b3);
  and and_16 (and_16_out, not_44_out, not_45_out, not_46_out, not_47_out, b4);
  and and_17 (and_17_out, b0, not_48_out, not_49_out, not_50_out, b4);
  and and_18 (and_18_out, not_51_out, b1, not_52_out, not_53_out, b4);
  and and_19 (and_19_out, b0, b1, not_54_out, not_55_out, b4);
  not not_56 (not_56_out, and_2_out);
  // AND_Gate and_20 has open pins: out=and_20_out
  not not_57 (not_57_out, xnor_1_out);
  xnor xnor_1 (xnor_1_out, and_1_out, not_56_out);
  not not_58 (not_58_out, and_20_out);
  xnor xnor_2 (xnor_2_out, not_57_out, and_3_out);
  not not_59 (not_59_out, and_3_out);
  not not_60 (not_60_out, and_4_out);
  // XNOR_Gate xnor_3 has open pins: in0=not_58_out, in1=undriven, out=open
  not not_61 (not_61_out, xnor_2_out);
  xnor xnor_4 (xnor_4_out, not_59_out, and_4_out);
  xnor xnor_5 (xnor_5_out, not_60_out, and_5_out);
  xnor xnor_6 (xnor_6_out, not_61_out, and_4_out);
  not not_62 (not_62_out, xnor_6_out);
  not not_63 (not_63_out, xnor_7_out);
  xnor xnor_7 (xnor_7_out, not_62_out, and_5_out);
  not not_64 (not_64_out, and_2_out);
  not not_65 (not_65_out, xnor_4_out);
  xnor xnor_8 (xnor_8_out, not_63_out, and_6_out);
  xnor xnor_9 (xnor_9_out, not_64_out, and_6_out);
  xnor xnor_10 (xnor_10_out, not_65_out, and_6_out);
  not not_66 (not_66_out, xnor_8_out);
  not not_67 (not_67_out, xnor_9_out);
  not not_68 (not_68_out, xnor_10_out);
  not not_69 (not_69_out, xnor_5_out);
  xnor xnor_11 (xnor_11_out, not_66_out, and_7_out);
  xnor xnor_12 (xnor_12_out, not_67_out, and_7_out);
  xnor xnor_13 (xnor_13_out, not_68_out, and_7_out);
  xnor xnor_14 (xnor_14_out, not_69_out, and_7_out);
  not not_70 (not_70_out, xnor_11_out);
  not not_71 (not_71_out, xnor_12_out);
  not not_72 (not_72_out, xnor_14_out);
  xnor xnor_15 (xnor_15_out, not_70_out, and_8_out);
  xnor xnor_16 (xnor_16_out, not_71_out, and_8_out);
  not not_73 (not_73_out, xnor_13_out);
  xnor xnor_17 (xnor_17_out, not_72_out, and_8_out);
  not not_74 (not_74_out, xnor_16_out);
  not not_75 (not_75_out, xnor_18_out);
  xnor xnor_18 (xnor_18_out, not_74_out, and_9_out);
  xnor xnor_19 (xnor_19_out, not_73_out, and_9_out);
  xnor xnor_20 (xnor_20_out, not_75_out, and_10_out);
  not not_76 (not_76_out, xnor_19_out);
  not not_77 (not_77_out, xnor_17_out);
  not not_78 (not_78_out, xnor_15_out);
  xnor xnor_21 (xnor_21_out, not_76_out, and_10_out);
  xnor xnor_22 (xnor_22_out, not_77_out, and_10_out);
  xnor xnor_23 (xnor_23_out, not_78_out, and_11_out);
  not not_79 (not_79_out, xnor_23_out);
  not not_80 (not_80_out, xnor_20_out);
  not not_81 (not_81_out, and_11_out);
  xnor xnor_24 (xnor_24_out, not_79_out, and_12_out);
  xnor xnor_25 (xnor_25_out, not_80_out, and_12_out);
  xnor xnor_26 (xnor_26_out, not_81_out, and_12_out);
  not not_82 (not_82_out, xnor_24_out);
  not not_83 (not_83_out, xnor_21_out);
  not not_84 (not_84_out, xnor_26_out);
  not not_85 (not_85_out, xnor_27_out);
  xnor xnor_27 (xnor_27_out, not_82_out, and_13_out);
  xnor xnor_28 (xnor_28_out, not_83_out, and_13_out);
  xnor xnor_29 (xnor_29_out, not_84_out, and_13_out);
  xnor xnor_30 (xnor_30_out, not_85_out, and_14_out);
  not not_86 (not_86_out, xnor_28_out);
  not not_87 (not_87_out, xnor_22_out);
  not not_88 (not_88_out, xnor_29_out);
  not not_89 (not_89_out, xnor_30_out);
  xnor xnor_31 (xnor_31_out, not_86_out, and_14_out);
  not not_90 (not_90_out, xnor_32_out);
  xnor xnor_32 (xnor_32_out, not_87_out, and_14_out);
  xnor xnor_33 (xnor_33_out, not_88_out, and_14_out);
  xnor xnor_34 (xnor_34_out, not_89_out, and_15_out);
  xnor xnor_35 (xnor_35_out, not_90_out, and_15_out);
  not not_91 (not_91_out, xnor_33_out);
  not not_92 (not_92_out, xnor_34_out);
  xnor xnor_36 (xnor_36_out, not_91_out, and_15_out);
  xnor xnor_37 (xnor_37_out, not_92_out, and_16_out);
  not not_93 (not_93_out, xnor_25_out);
  not not_94 (not_94_out, xnor_31_out);
  not not_95 (not_95_out, xnor_36_out);
  xnor xnor_38 (xnor_38_out, not_93_out, and_16_out);
  xnor xnor_39 (xnor_39_out, not_94_out, and_16_out);
  xnor xnor_40 (xnor_40_out, not_95_out, and_16_out);
  not not_96 (not_96_out, xnor_37_out);
  not not_97 (not_97_out, xnor_38_out);
  not not_98 (not_98_out, xnor_39_out);
  not not_99 (not_99_out, xnor_35_out);
  not not_100 (not_100_out, xnor_40_out);
  xnor xnor_41 (xnor_41_out, not_96_out, and_17_out);
  xnor xnor_42 (xnor_42_out, not_97_out, and_17_out);
  xnor xnor_43 (xnor_43_out, not_98_out, and_17_out);
  xnor xnor_44 (xnor_44_out, not_99_out, and_17_out);
  xnor xnor_45 (xnor_45_out, not_100_out, and_17_out);
  not not_101 (not_101_out, xnor_41_out);
  not not_102 (not_102_out, xnor_42_out);
  not not_103 (not_103_out, xnor_44_out);
  xnor xnor_46 (out_7, not_101_out, and_18_out);
  xnor xnor_47 (xnor_47_out, not_102_out, and_18_out);
  xnor xnor_48 (out_10, not_103_out, and_18_out);
  not not_104 (not_104_out, xnor_45_out);
  not not_105 (not_105_out, xnor_47_out);
  not not_106 (not_106_out, xnor_43_out);
  xnor xnor_49 (xnor_49_out, not_104_out, and_18_out);
  xnor xnor_50 (out_8, not_105_out, and_19_out);
  xnor xnor_51 (out_9, not_106_out, and_19_out);
  not not_107 (not_107_out, xnor_49_out);
  xnor xnor_52 (out_11, not_107_out, and_19_out);

  // Notes on the sheet:
  //   A | 1
  //   B | 12
  //   C | 14
  //   D | 145
  //   E | 15
  //   F | 124
  //   G | 1245
  //   H | 125
  //   I | 24
  //   J | 245
  //   K | 13
  //   L | 123
  //   M | 134
  //   N | 1345
  //   O | 135
  //   P | 1234
  //   Q | 12345
  //   R | 1235
  //   S | 234
  //   1
  //   2
  //   4
  //   5
  //   3
  //   pinos
  //   pinos
  //   1
  //   2
  //   4
  //   5
  //   3
endmodule
